# Fritzing sketch Robot Arm Wiring (saved by Fritzing 1.0.4)

parts:
  Part1 = Arduino Uno (Rev3)
  J1 = Basic Servo
  J2 = Basic Servo
  J3 = Basic Servo
  J4 = Basic Servo
  J5 = Basic Servo
  J6 = Basic Servo
  Part2 = Adafruit PCA9685 PWM/Servo Breakout [part_number=815]
  U1 = LM2596 step down module
  C1 = Electrolytic Capacitor [capacitance=4.7mF voltage=16V package="100 mil [THT, electrolytic]"]

nets:
  N1: Part1.A4/SDA, Part2.SDA
  N2: Part1.A5/SCL, Part2.SCL
  5V: Part1.5V, Part2.VCC
  GND: Part1.GND, J1.gnd, J2.gnd, J3.gnd, J4.gnd, J5.gnd, J6.gnd, Part2.GND, U1.IN-, U1.OUT-, C1.-
  VCC: J1.vcc, J2.vcc, J3.vcc, J4.vcc, J5.vcc, J6.vcc, Part2.5.0V
  N3: J1.pulse, Part2.PWM0
  N4: J2.pulse, Part2.PWM9
  N5: J3.pulse, Part2.PWM12
  N6: J4.pulse, Part2.PWM6
  N7: J5.pulse, Part2.PWM15
  N8: J6.pulse, Part2.PWM3
  N9: Part2.PWRIN, U1.OUT+, C1.+

custom parts:
  Adafruit PCA9685 PWM/Servo Breakout: Using only two pins, control 16 free-running PWM outputs! I2C-controlled PWM driver with a built in clock. Unlike the TLC5940 family, you do not need to continuously send it signal tying up your microcontroller, its completely free running! 5V compliant, which means you can control it from a 3.3V microcontroller and still safely drive up to 6V outputs (this is good for when you want to control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
  LM2596 step down module: LM2596 DC-DC step down power supply module 3 A.
